// Logisim project my_circ.circ as structural Verilog: 1 circuit, main circuit main
module main (
  input  A,
  input  B,
  input  C,
  input  D,
  output Y,
  output Z
);

  wire nand_1_out, nor_1_out, not_1_out, or_1_out;

  not not_1 (not_1_out, D);
  or or_1 (or_1_out, A, B);
  nand nand_1 (nand_1_out, C, not_1_out);
  nor nor_1 (nor_1_out, B, D);
  xor xor_1 (Z, nand_1_out, nor_1_out);
  xnor xnor_1 (Y, or_1_out, nand_1_out);
endmodule
